// Logisim project 74.circ as structural Verilog: 1 circuit, main circuit main
module main (
  input  [15:0] ADDRESS
);

  wire adder_1_cout, ALU_INVERT, B_pin12, B_pin15, B_pin16, B_pin19, BP_CD, BP_CU, BP_H_WE, BP_L_WE, C_IN,
       C_OUT, CLK, n7485_1_pin2, n7485_1_pin3, n7485_1_pin4, n7485_1_pin5, n7485_1_pin6, n7485_1_pin7,
       n7486_1_pin1, n7486_1_pin4, n7486_1_pin10, n7486_1_pin13, n74193_1_pin4, n74193_1_pin5,
       n74193_1_pin11, n74193_1_pin12, n74193_1_pin13, n74193_2_pin12, n74193_2_pin13, n74193_3_pin11,
       n74193_3_pin12, n74193_3_pin13, n74245_1_pin1, n74245_1_pin11, n74245_1_pin12, n74245_1_pin13,
       n74245_1_pin14, n74245_1_pin15, n74245_1_pin16, n74245_1_pin17, n74245_1_pin18, n74245_2_pin1,
       n74245_2_pin11, n74245_2_pin12, n74245_2_pin13, n74245_2_pin14, n74245_2_pin15, n74245_2_pin16,
       n74245_2_pin17, n74245_2_pin18, n74245_3_pin1, n74245_3_pin11, n74245_3_pin12, n74245_3_pin13,
       n74245_3_pin14, n74245_3_pin15, n74245_3_pin16, n74245_3_pin17, n74245_3_pin18, n74245_4_pin1,
       n74245_4_pin11, n74245_4_pin12, n74245_4_pin13, n74245_4_pin14, n74245_4_pin15, n74245_4_pin16,
       n74245_4_pin17, n74245_4_pin18, n74245_5_pin1, n74245_5_pin11, n74245_5_pin12, n74245_5_pin13,
       n74245_5_pin14, n74245_5_pin15, n74245_5_pin16, n74245_5_pin17, n74245_5_pin18, n74245_6_pin1,
       n74245_6_pin11, n74245_6_pin12, n74245_6_pin13, n74245_6_pin14, n74245_6_pin15, n74245_6_pin16,
       n74245_6_pin17, n74245_6_pin18, n74245_7_pin1, n74245_8_pin1, n74283_1_pin1, n74283_1_pin2,
       n74283_1_pin4, n74283_1_pin6, n74283_1_pin9, n74283_1_pin10, n74283_1_pin11, n74283_1_pin13,
       n74283_1_pin15, n74283_2_pin1, n74283_2_pin2, n74283_2_pin4, n74283_2_pin6, n74283_2_pin10,
       n74283_2_pin11, n74283_2_pin13, n74283_2_pin15, nA_H_OE, nA_L_OE, nB_WE, nBP_OE, nPC_OE, nSP_OE,
       PC_CD, PC_CU, PC_H_WE, PC_HL_pin11, PC_HL_pin12, PC_HL_pin13, PC_L_WE, PC_LH_pin12, PC_LH_pin13,
       PC_LL_pin4, PC_LL_pin5, PC_LL_pin11, PC_LL_pin12, PC_LL_pin13, RESET, SP_CD, SP_CU, SP_H_WE,
       SP_HL_pin11, SP_HL_pin12, SP_HL_pin13, SP_L_WE, SP_LH_pin12, SP_LH_pin13, SP_LL_pin4, SP_LL_pin5,
       SP_LL_pin11, SP_LL_pin12, SP_LL_pin13;
  wire [3:0] n7485_1_pin9, n7485_1_pin10;
  wire [7:0] adder_1_out, n74245_7_pin18, pull_resistor_2_node;

  _74245 #(.ShowInternalStructure("true")) u_74245_1 (
    .pin1(n74245_1_pin1), .pin2(ADDRESS[0]), .pin3(ADDRESS[1]), .pin4(ADDRESS[2]), .pin5(ADDRESS[3]),
    .pin6(ADDRESS[4]), .pin7(ADDRESS[5]), .pin8(ADDRESS[6]), .pin9(ADDRESS[7]), .pin19(nPC_OE),
    .pin18(n74245_1_pin18), .pin17(n74245_1_pin17), .pin16(n74245_1_pin16), .pin15(n74245_1_pin15),
    .pin14(n74245_1_pin14), .pin13(n74245_1_pin13), .pin12(n74245_1_pin12), .pin11(n74245_1_pin11));
  _74245 #(.ShowInternalStructure("true")) u_74245_2 (
    .pin1(n74245_2_pin1), .pin2(ADDRESS[8]), .pin3(ADDRESS[9]), .pin4(ADDRESS[10]), .pin5(ADDRESS[11]),
    .pin6(ADDRESS[12]), .pin7(ADDRESS[13]), .pin8(ADDRESS[14]), .pin9(ADDRESS[15]), .pin19(nPC_OE),
    .pin18(n74245_2_pin18), .pin17(n74245_2_pin17), .pin16(n74245_2_pin16), .pin15(n74245_2_pin15),
    .pin14(n74245_2_pin14), .pin13(n74245_2_pin13), .pin12(n74245_2_pin12), .pin11(n74245_2_pin11));
  _74245 #(.ShowInternalStructure("true")) u_74245_3 (
    .pin1(n74245_3_pin1), .pin2(ADDRESS[0]), .pin3(ADDRESS[1]), .pin4(ADDRESS[2]), .pin5(ADDRESS[3]),
    .pin6(ADDRESS[4]), .pin7(ADDRESS[5]), .pin8(ADDRESS[6]), .pin9(ADDRESS[7]), .pin19(nSP_OE),
    .pin18(n74245_3_pin18), .pin17(n74245_3_pin17), .pin16(n74245_3_pin16), .pin15(n74245_3_pin15),
    .pin14(n74245_3_pin14), .pin13(n74245_3_pin13), .pin12(n74245_3_pin12), .pin11(n74245_3_pin11));
  _74245 #(.ShowInternalStructure("true")) u_74245_4 (
    .pin1(n74245_4_pin1), .pin2(ADDRESS[8]), .pin3(ADDRESS[9]), .pin4(ADDRESS[10]), .pin5(ADDRESS[11]),
    .pin6(ADDRESS[12]), .pin7(ADDRESS[13]), .pin8(ADDRESS[14]), .pin9(ADDRESS[15]), .pin19(nSP_OE),
    .pin18(n74245_4_pin18), .pin17(n74245_4_pin17), .pin16(n74245_4_pin16), .pin15(n74245_4_pin15),
    .pin14(n74245_4_pin14), .pin13(n74245_4_pin13), .pin12(n74245_4_pin12), .pin11(n74245_4_pin11));
  _74245 #(.ShowInternalStructure("true")) u_74245_5 (
    .pin1(n74245_5_pin1), .pin2(ADDRESS[0]), .pin3(ADDRESS[1]), .pin4(ADDRESS[2]), .pin5(ADDRESS[3]),
    .pin6(ADDRESS[4]), .pin7(ADDRESS[5]), .pin8(ADDRESS[6]), .pin9(ADDRESS[7]), .pin19(nBP_OE),
    .pin18(n74245_5_pin18), .pin17(n74245_5_pin17), .pin16(n74245_5_pin16), .pin15(n74245_5_pin15),
    .pin14(n74245_5_pin14), .pin13(n74245_5_pin13), .pin12(n74245_5_pin12), .pin11(n74245_5_pin11));
  _74245 #(.ShowInternalStructure("true")) u_74245_6 (
    .pin1(n74245_6_pin1), .pin2(ADDRESS[8]), .pin3(ADDRESS[9]), .pin4(ADDRESS[10]), .pin5(ADDRESS[11]),
    .pin6(ADDRESS[12]), .pin7(ADDRESS[13]), .pin8(ADDRESS[14]), .pin9(ADDRESS[15]), .pin19(nBP_OE),
    .pin18(n74245_6_pin18), .pin17(n74245_6_pin17), .pin16(n74245_6_pin16), .pin15(n74245_6_pin15),
    .pin14(n74245_6_pin14), .pin13(n74245_6_pin13), .pin12(n74245_6_pin12), .pin11(n74245_6_pin11));
  _74245 #(.ShowInternalStructure("true")) u_74245_7 (
    .pin1(n74245_7_pin1), .pin2(ADDRESS[0]), .pin3(ADDRESS[1]), .pin4(ADDRESS[2]), .pin5(ADDRESS[3]),
    .pin6(ADDRESS[4]), .pin7(ADDRESS[5]), .pin8(ADDRESS[6]), .pin9(ADDRESS[7]), .pin19(nA_L_OE),
    .pin18(n74245_7_pin18[0]), .pin17(n74245_7_pin18[1]), .pin16(n74245_7_pin18[2]),
    .pin15(n74245_7_pin18[3]), .pin14(n74245_7_pin18[4]), .pin13(n74245_7_pin18[5]),
    .pin12(n74245_7_pin18[6]), .pin11(n74245_7_pin18[7]));
  _74245 #(.ShowInternalStructure("true")) u_74245_8 (
    .pin1(n74245_8_pin1), .pin2(ADDRESS[8]), .pin3(ADDRESS[9]), .pin4(ADDRESS[10]), .pin5(ADDRESS[11]),
    .pin6(ADDRESS[12]), .pin7(ADDRESS[13]), .pin8(ADDRESS[14]), .pin9(ADDRESS[15]), .pin19(nA_H_OE),
    .pin18(n74245_7_pin18[0]), .pin17(n74245_7_pin18[1]), .pin16(n74245_7_pin18[2]),
    .pin15(n74245_7_pin18[3]), .pin14(n74245_7_pin18[4]), .pin13(n74245_7_pin18[5]),
    .pin12(n74245_7_pin18[6]), .pin11(n74245_7_pin18[7]));
  _74193 #(.ShowInternalStructure("true")) PC_LL (
    .pin1(n74245_7_pin18[1]), .pin2(n74245_1_pin17), .pin3(n74245_1_pin18), .pin4(PC_LL_pin4),
    .pin5(PC_LL_pin5), .pin6(n74245_1_pin16), .pin7(n74245_1_pin15), .pin15(n74245_7_pin18[0]),
    .pin14(RESET), .pin13(PC_LL_pin13), .pin12(PC_LL_pin12), .pin11(PC_LL_pin11), .pin10(n74245_7_pin18[2]),
    .pin9(n74245_7_pin18[3]));
  _74193 #(.ShowInternalStructure("true")) PC_LH (
    .pin1(n74245_7_pin18[5]), .pin2(n74245_1_pin13), .pin3(n74245_1_pin14), .pin4(PC_LL_pin13),
    .pin5(PC_LL_pin12), .pin6(n74245_1_pin12), .pin7(n74245_1_pin11), .pin15(n74245_7_pin18[4]),
    .pin14(RESET), .pin13(PC_LH_pin13), .pin12(PC_LH_pin12), .pin11(PC_LL_pin11), .pin10(n74245_7_pin18[6]),
    .pin9(n74245_7_pin18[7]));
  _74193 #(.ShowInternalStructure("true")) PC_HL (
    .pin1(n74245_7_pin18[1]), .pin2(n74245_2_pin17), .pin3(n74245_2_pin18), .pin4(PC_LH_pin13),
    .pin5(PC_LH_pin12), .pin6(n74245_2_pin16), .pin7(n74245_2_pin15), .pin15(n74245_7_pin18[0]),
    .pin14(RESET), .pin13(PC_HL_pin13), .pin12(PC_HL_pin12), .pin11(PC_HL_pin11), .pin10(n74245_7_pin18[2]),
    .pin9(n74245_7_pin18[3]));
  _74193 #(.ShowInternalStructure("true")) PC_HH (
    .pin1(n74245_7_pin18[5]), .pin2(n74245_2_pin13), .pin3(n74245_2_pin14), .pin4(PC_HL_pin13),
    .pin5(PC_HL_pin12), .pin6(n74245_2_pin12), .pin7(n74245_2_pin11), .pin15(n74245_7_pin18[4]),
    .pin14(RESET), .pin11(PC_HL_pin11), .pin10(n74245_7_pin18[6]), .pin9(n74245_7_pin18[7]));  // open: pin13, pin12
  _7400 #(.ShowInternalStructure("true")) u_7400_1 (
    .pin1(PC_CU), .pin2(CLK), .pin3(PC_LL_pin5), .pin4(PC_CD), .pin5(CLK), .pin6(PC_LL_pin4),
    .pin13(PC_H_WE), .pin12(CLK), .pin11(PC_HL_pin11), .pin10(PC_L_WE), .pin9(CLK), .pin8(PC_LL_pin11));
  _74193 #(.ShowInternalStructure("true")) SP_LL (
    .pin1(n74245_7_pin18[1]), .pin2(n74245_3_pin17), .pin3(n74245_3_pin18), .pin4(SP_LL_pin4),
    .pin5(SP_LL_pin5), .pin6(n74245_3_pin16), .pin7(n74245_3_pin15), .pin15(n74245_7_pin18[0]),
    .pin14(RESET), .pin13(SP_LL_pin13), .pin12(SP_LL_pin12), .pin11(SP_LL_pin11), .pin10(n74245_7_pin18[2]),
    .pin9(n74245_7_pin18[3]));
  _74193 #(.ShowInternalStructure("true")) SP_LH (
    .pin1(n74245_7_pin18[5]), .pin2(n74245_3_pin13), .pin3(n74245_3_pin14), .pin4(SP_LL_pin13),
    .pin5(SP_LL_pin12), .pin6(n74245_3_pin12), .pin7(n74245_3_pin11), .pin15(n74245_7_pin18[4]),
    .pin14(RESET), .pin13(SP_LH_pin13), .pin12(SP_LH_pin12), .pin11(SP_LL_pin11), .pin10(n74245_7_pin18[6]),
    .pin9(n74245_7_pin18[7]));
  _74193 #(.ShowInternalStructure("true")) SP_HL (
    .pin1(n74245_7_pin18[1]), .pin2(n74245_4_pin17), .pin3(n74245_4_pin18), .pin4(SP_LH_pin13),
    .pin5(SP_LH_pin12), .pin6(n74245_4_pin16), .pin7(n74245_4_pin15), .pin15(n74245_7_pin18[0]),
    .pin14(RESET), .pin13(SP_HL_pin13), .pin12(SP_HL_pin12), .pin11(SP_HL_pin11), .pin10(n74245_7_pin18[2]),
    .pin9(n74245_7_pin18[3]));
  _74193 #(.ShowInternalStructure("true")) SP_HH (
    .pin1(n74245_7_pin18[5]), .pin2(n74245_4_pin13), .pin3(n74245_4_pin14), .pin4(SP_HL_pin13),
    .pin5(SP_HL_pin12), .pin6(n74245_4_pin12), .pin7(n74245_4_pin11), .pin15(n74245_7_pin18[4]),
    .pin14(RESET), .pin11(SP_HL_pin11), .pin10(n74245_7_pin18[6]), .pin9(n74245_7_pin18[7]));  // open: pin13, pin12
  _7400 #(.ShowInternalStructure("true")) u_7400_2 (
    .pin1(SP_CU), .pin2(CLK), .pin3(SP_LL_pin5), .pin4(SP_CD), .pin5(CLK), .pin6(SP_LL_pin4),
    .pin13(SP_H_WE), .pin12(CLK), .pin11(SP_HL_pin11), .pin10(SP_L_WE), .pin9(CLK), .pin8(SP_LL_pin11));
  _74193 #(.ShowInternalStructure("true")) u_74193_1 (
    .pin1(n74245_7_pin18[1]), .pin2(n74245_5_pin17), .pin3(n74245_5_pin18), .pin4(n74193_1_pin4),
    .pin5(n74193_1_pin5), .pin6(n74245_5_pin16), .pin7(n74245_5_pin15), .pin15(n74245_7_pin18[0]),
    .pin14(RESET), .pin13(n74193_1_pin13), .pin12(n74193_1_pin12), .pin11(n74193_1_pin11),
    .pin10(n74245_7_pin18[2]), .pin9(n74245_7_pin18[3]));
  _74193 #(.ShowInternalStructure("true")) u_74193_2 (
    .pin1(n74245_7_pin18[5]), .pin2(n74245_5_pin13), .pin3(n74245_5_pin14), .pin4(n74193_1_pin13),
    .pin5(n74193_1_pin12), .pin6(n74245_5_pin12), .pin7(n74245_5_pin11), .pin15(n74245_7_pin18[4]),
    .pin14(RESET), .pin13(n74193_2_pin13), .pin12(n74193_2_pin12), .pin11(n74193_1_pin11),
    .pin10(n74245_7_pin18[6]), .pin9(n74245_7_pin18[7]));
  _74193 #(.ShowInternalStructure("true")) u_74193_3 (
    .pin1(n74245_7_pin18[1]), .pin2(n74245_6_pin17), .pin3(n74245_6_pin18), .pin4(n74193_2_pin13),
    .pin5(n74193_2_pin12), .pin6(n74245_6_pin16), .pin7(n74245_6_pin15), .pin15(n74245_7_pin18[0]),
    .pin14(RESET), .pin13(n74193_3_pin13), .pin12(n74193_3_pin12), .pin11(n74193_3_pin11),
    .pin10(n74245_7_pin18[2]), .pin9(n74245_7_pin18[3]));
  _74193 #(.ShowInternalStructure("true")) u_74193_4 (
    .pin1(n74245_7_pin18[5]), .pin2(n74245_6_pin13), .pin3(n74245_6_pin14), .pin4(n74193_3_pin13),
    .pin5(n74193_3_pin12), .pin6(n74245_6_pin12), .pin7(n74245_6_pin11), .pin15(n74245_7_pin18[4]),
    .pin14(RESET), .pin11(n74193_3_pin11), .pin10(n74245_7_pin18[6]), .pin9(n74245_7_pin18[7]));  // open: pin13, pin12
  _7400 #(.ShowInternalStructure("true")) u_7400_3 (
    .pin1(BP_CU), .pin2(CLK), .pin3(n74193_1_pin5), .pin4(BP_CD), .pin5(CLK), .pin6(n74193_1_pin4),
    .pin13(BP_H_WE), .pin12(CLK), .pin11(n74193_3_pin11), .pin10(BP_L_WE), .pin9(CLK), .pin8(n74193_1_pin11));
  Pull_Resistor pull_resistor_1 (.node(n74245_7_pin18));
  Pull_Resistor pull_resistor_2 (.node(pull_resistor_2_node));
  _74283 #(.ShowInternalStructure("true")) u_74283_1 (
    .pin1(n74283_1_pin1), .pin2(n74283_1_pin2), .pin3(pull_resistor_2_node[1]), .pin4(n74283_1_pin4),
    .pin5(pull_resistor_2_node[0]), .pin6(n74283_1_pin6), .pin7(C_IN), .pin15(n74283_1_pin15),
    .pin14(pull_resistor_2_node[2]), .pin13(n74283_1_pin13), .pin12(pull_resistor_2_node[3]),
    .pin11(n74283_1_pin11), .pin10(n74283_1_pin10), .pin9(n74283_1_pin9));
  _7486 #(.ShowInternalStructure("true")) u_7486_1 (
    .pin1(n7486_1_pin1), .pin2(ALU_INVERT), .pin3(n74283_1_pin2), .pin4(n7486_1_pin4), .pin5(ALU_INVERT),
    .pin6(n74283_1_pin6), .pin13(n7486_1_pin13), .pin12(ALU_INVERT), .pin11(n74283_1_pin15),
    .pin10(n7486_1_pin10), .pin9(ALU_INVERT), .pin8(n74283_1_pin11));
  _7485 #(.ShowInternalStructure("true")) u_7485_1 (
    .pin1(n7485_1_pin9[3]), .pin2(n7485_1_pin2), .pin3(n7485_1_pin3), .pin4(n7485_1_pin4),
    .pin5(n7485_1_pin5), .pin6(n7485_1_pin6), .pin7(n7485_1_pin7), .pin15(n7485_1_pin10[3]),
    .pin14(n7485_1_pin9[2]), .pin13(n7485_1_pin10[2]), .pin12(n7485_1_pin10[1]), .pin11(n7485_1_pin9[1]),
    .pin10(n7485_1_pin10[0]), .pin9(n7485_1_pin9[0]));
  _74139 #(.ShowInternalStructure("true")) u_74139_1 ();  // open: pin1, pin2, pin3, pin4, pin5, pin6, pin7, pin15, pin14, pin13, pin12, pin11, pin10, pin9
  Button button_1 (.out(PC_L_WE));
  Button button_2 (.out(PC_H_WE));
  Button button_3 (.out(PC_CU));
  Button button_4 (.out(PC_CD));
  Button #(.press("passive")) button_5 (.out(nPC_OE));
  Button button_6 (.out(SP_L_WE));
  Button button_7 (.out(SP_H_WE));
  Button button_8 (.out(SP_CU));
  Button button_9 (.out(SP_CD));
  Button #(.press("passive")) button_10 (.out(nSP_OE));
  Button button_11 (.out(BP_L_WE));
  Button button_12 (.out(BP_H_WE));
  Button button_13 (.out(BP_CU));
  Button button_14 (.out(BP_CD));
  Button #(.press("passive")) button_15 (.out(nBP_OE));
  Button #(.press("passive")) button_16 (.out(nA_L_OE));
  Button #(.press("passive")) button_17 (.out(nA_H_OE));
  Button button_18 (.out(RESET));
  Clock clock_1 (.out(CLK));
  Button button_19 (.out(n7485_1_pin2));
  Button #(.press("passive")) button_20 (.out(n7485_1_pin3));
  Button button_21 (.out(n7485_1_pin4));
  LED led_1 (.in(n7485_1_pin5));
  _74377 #(.ShowInternalStructure("true")) B (
    .pin1(nB_WE), .pin2(n7486_1_pin4), .pin3(pull_resistor_2_node[0]), .pin4(pull_resistor_2_node[1]),
    .pin5(n7486_1_pin1), .pin6(n7486_1_pin13), .pin7(pull_resistor_2_node[2]),
    .pin8(pull_resistor_2_node[3]), .pin9(n7486_1_pin10), .pin19(B_pin19), .pin18(pull_resistor_2_node[7]),
    .pin17(pull_resistor_2_node[6]), .pin16(B_pin16), .pin15(B_pin15), .pin14(pull_resistor_2_node[5]),
    .pin13(pull_resistor_2_node[4]), .pin12(B_pin12), .pin11(CLK));
  LED led_2 (.in(n7485_1_pin6));
  LED led_3 (.in(n7485_1_pin7));
  _74138 #(.ShowInternalStructure("true")) u_74138_1 ();  // open: pin1, pin2, pin3, pin4, pin5, pin6, pin7, pin15, pin14, pin13, pin12, pin11, pin10, pin9
  _74283 #(.ShowInternalStructure("true")) u_74283_2 (
    .pin1(n74283_2_pin1), .pin2(n74283_2_pin2), .pin3(pull_resistor_2_node[5]), .pin4(n74283_2_pin4),
    .pin5(pull_resistor_2_node[4]), .pin6(n74283_2_pin6), .pin7(n74283_1_pin9), .pin15(n74283_2_pin15),
    .pin14(pull_resistor_2_node[6]), .pin13(n74283_2_pin13), .pin12(pull_resistor_2_node[7]),
    .pin11(n74283_2_pin11), .pin10(n74283_2_pin10), .pin9(C_OUT));
  _7486 #(.ShowInternalStructure("true")) u_7486_2 (
    .pin1(B_pin15), .pin2(ALU_INVERT), .pin3(n74283_2_pin2), .pin4(B_pin12), .pin5(ALU_INVERT),
    .pin6(n74283_2_pin6), .pin13(B_pin16), .pin12(ALU_INVERT), .pin11(n74283_2_pin15), .pin10(B_pin19),
    .pin9(ALU_INVERT), .pin8(n74283_2_pin11));
  Button button_22 (.out(ALU_INVERT));
  Button button_23 (.out(C_IN));
  Button #(.press("passive")) button_24 (.out(nB_WE));
  Adder adder_1 (.a(8'h80), .b(8'h80), .out(adder_1_out), .cin(adder_1_cout), .cout(adder_1_cout));
  // Probe on adder_1_out
  // also tied to GND on the sheet: {n74245_1_pin1, n74245_2_pin1, n74245_3_pin1, n74245_4_pin1, n74245_5_pin1, n74245_6_pin1, n7485_1_pin10[1], n7485_1_pin10[3], n7485_1_pin9[1], n7485_1_pin9[3]}
  // also tied to VCC on the sheet: {n74245_7_pin1, n74245_8_pin1, n7485_1_pin10[0], n7485_1_pin10[2], n7485_1_pin9[0], n7485_1_pin9[2]}

  // Notes on the sheet:
  //   ADDRESS: pull=down
endmodule
